# Fritzing sketch Timer_rele_7LED (saved by Fritzing 0.9.3b)
breadboards: 1

parts:
  Part1 = Arduino Uno (Rev3)
  S1 = Pushbutton [package="[THT]"]
  R1 = Resistor [tolerance=±5% resistance=10k package=THT]
  KY-1 = Keyes Relay [package=THT]
  R2 = Resistor [tolerance=±5% resistance=220 package=THT]
  DI2 = 7-Segment LED Display [package=THT]
  LED1 = LEDs [package=led10mm]

nets:
  N1: Part1.D8, DI2.cathodeD
  N2: Part1.D9_PWM, DI2.cathodeE
  N3: Part1.D10_PWM/SS, DI2.cathodeF
  N4: Part1.D11_PWM/MOSI, DI2.cathodeG
  N5: Part1.D12/MISO, KY-1.signal
  N6: Part1.D2, S1.Pin_1, S1.Pin_2, R1.Pin_0
  N7: Part1.D4, DI2.cathodeDP
  N8: Part1.D5_PWM, DI2.cathodeA
  N9: Part1.D6_PWM, DI2.cathodeB
  N10: Part1.D7, DI2.cathodeC
  N11: Part1.5V, S1.Pin_3, S1.Pin_4, KY-1.power, R2.Pin_1
  N12: Part1.GND, R1.Pin_1, KY-1.ground
  N13: KY-1.NO, LED1.C
  N14: R2.Pin_0, DI2.commAnode#2

notes:
  Wall supply power

custom parts:
  Keyes Relay: The Keyes 5V relay module is suitable for SCM development, home appliance control. It uses a 5V~12V TIL control signal which can control DC / AC signal.
  LEDs: LEDs Standard schematic elements and footprints for 5mm, 3mm, 1206, and 0603 sized LEDs. 5mm - Spark Fun Electronics SKU : COM-00529 (and others)

// code stored in the sketch: Timer_rele_7LED.ino

//Library
#include "SevenSeg.h"

// constants won't change. They're used here to set pin numbers:
const int buttonPin = 2;     // the number of the pushbutton pin
const int relePin = 12;     // Rele variables
const int dotPin = 4;

//Defines the segments A-G: SevenSeg(A, B, C, D, E, F, G);
SevenSeg disp (5,6,7,8,9,10,11);
const int numOfDigits = 1;  //Number of 7 segments
int digitPins [numOfDigits]={4};  //CC(or CA) pins of segment

//Variables
int _number = 0; //Default number

// variables will change:
int _buttonState = 0;         // variable for reading the pushbutton status

//timer variables
int _count = 0; // number of pushing the button

long int _timing = 0;
long int _timingButton = 0;
long int _initButtonTiming = 0;

// Contant that won't change
const long int _timeScale_ = 600000; // 10min each unit
const int _blinkTimer_ = 500; // timing for dot blinking
long int _delayReadingButton_ = 2000;




// SET UP --------------------------------------------------------------

void setup() {
  
  Serial.begin(9600);

  // initialize the pushbutton pin as an input:
  pinMode(buttonPin, INPUT);
  
  //Defines the number of digits to be "numOfDigits" and the digit pins to be the elements of the array "digitPins"
  // disp.setDigitPins ( numOfDigits , digitPins ); // We spare one pin conecting directly sour 5V
  //Only for common cathode 7segments
  disp.setCommonAnode();
  //Control brightness (values 0-100);
  disp.setDutyCycle(50);
  disp.setDPPin(dotPin);

  //Rele
  pinMode(relePin, OUTPUT);
  releON(false);
  
}

// ----------------------------------------------------------- END SET UP


void updateLED(int n){
  if (n>=0 && n<=9){  //Valid range is from 0 to 9
    disp.writeDigit(n);  //Print number to 7 segment display
  }
  else {
    disp.clearDisp();
  }
}

bool isButtonPressed(){
  // read the state of the pushbutton value:
  _buttonState = digitalRead(buttonPin);
  if (_buttonState == HIGH){
    disp.clearDP();
    return true;
  }
  return false;
}


bool blinkLED(bool up){
  if(up){
    disp.setDP();
    return false;
  }
  else{
    disp.clearDP();
    return true;
  }
}


void releON(bool s){
  if (s == true){
    digitalWrite(relePin, HIGH);
  }
  else{
    digitalWrite(relePin, LOW);
  }
}


void buttonWatcher(){
  // check if the pushbutton is pressed. If it is, the buttonState is HIGH:
  if (isButtonPressed()) {
    Serial.println("BUTTON PRESSED---------------------------------------");
    _initButtonTiming = millis();
    _count = _count + 1;
    updateLED(_count);
    if (_count == 10){
      _count = 0;
      updateLED(_count);
    }
    Serial.print("Count:"); Serial.println(_count);
    delay(200);
    while(_timingButton < _delayReadingButton_){
      buttonWatcher();
    }
    _timingButton = 0;
  }
  _timingButton = millis() - _initButtonTiming;
}

bool runTimer(){
  int stepTime = 10;
  bool light = true;
  long int t0 = 0;
  long int timer = 0;

  timer = _count * _timeScale_;
  t0 = timer;
  while (timer >= 0){
    if ((t0-timer)/_blinkTimer_ > 0){
      t0 = timer;
      light = blinkLED(light);
    }
    if (isButtonPressed()){
      Serial.println("Button pressed, exit from loop");
      buttonWatcher();
      break;
    }
    delay(stepTime);
    _count = timer/_timeScale_;
    updateLED(_count);
    timer = timer - stepTime;
  }
  Serial.println("runTimer ended");
  return true;
}

void loop()
{
  _count = -1;
  Serial.println("Init loop");
  Serial.print("Count: "); Serial.println(_count);

  buttonWatcher();

  if (_count > 0){
    releON(true);
    runTimer();
  }
  releON(false);
  _timingButton = 0;
  disp.clearDisp();
  Serial.println("End");
}
